# Fritzing sketch AVP (saved by Fritzing 0.9.3b)

parts:
  4x20_LCD_screen_w/Green_Screen1 = 4x20 LCD screen w/Green Screen
  kEYPAD_MATRICIAL_1 = KEYPAD 4x3
  LED1 = LED - 5mm [color="Green (570nm)" package="5 mm [THT]"]
  LED2 = LED - 5mm [color="Red (660nm)" package="5 mm [THT]"]
  R1 = Resistor [tolerance=±5% resistance=1k package=THT]
  R2 = Resistor [tolerance=±5% resistance=1k package=THT]
  Part1 = Arduino Mega 2560 (Rev3)
  J1 = Basic Servo
  J2 = Piezo Speaker
  LCM1602_IIC1 = LCM1602 IIC [part_number="LCM1602 IIC" chip_label="LCM1602 IIC" package="DIP (Dual Inline) [THT]"]
  Part2 = Arduino Mega 2560 (Rev3)
  4x20_LCD_screen_w/Green_Screen2 = 4x20 LCD screen w/Green Screen
  LED3 = LED - 5mm [color="Green (570nm)" package="5 mm [THT]"]
  LED4 = LED - 5mm [color="Red (660nm)" package="5 mm [THT]"]
  R3 = Resistor [tolerance=±5% resistance=1k package=THT]
  R4 = Resistor [tolerance=±5% resistance=1k package=THT]
  J3 = Basic Servo
  J4 = Piezo Speaker
  LCM1602_IIC2 = LCM1602 IIC [part_number="LCM1602 IIC" chip_label="LCM1602 IIC" package="DIP (Dual Inline) [THT]"]
  Keypad4x1 = Keypad Membran 4x4
  S1 = Square Pushbutton
  S2 = Square Pushbutton
  hc-sr2 = hc-sr04
  hc-sr3 = hc-sr04

nets:
  VSS: 4x20_LCD_screen_w/Green_Screen1.VSS, LCM1602_IIC1.VSS
  VDD: 4x20_LCD_screen_w/Green_Screen1.VDD, LCM1602_IIC1.VDD
  N1: 4x20_LCD_screen_w/Green_Screen1.V0, LCM1602_IIC1.V0
  N2: 4x20_LCD_screen_w/Green_Screen1.RS, LCM1602_IIC1.RS
  N3: 4x20_LCD_screen_w/Green_Screen1.R/W, LCM1602_IIC1.RW
  N4: 4x20_LCD_screen_w/Green_Screen1.E, LCM1602_IIC1.E
  N5: 4x20_LCD_screen_w/Green_Screen1.DB0, LCM1602_IIC1.D0
  N6: 4x20_LCD_screen_w/Green_Screen1.DB1, LCM1602_IIC1.D1
  N7: 4x20_LCD_screen_w/Green_Screen1.DB2, LCM1602_IIC1.D2
  N8: 4x20_LCD_screen_w/Green_Screen1.DB3, LCM1602_IIC1.D3
  N9: 4x20_LCD_screen_w/Green_Screen1.DB4, LCM1602_IIC1.D4
  N10: 4x20_LCD_screen_w/Green_Screen1.DB5, LCM1602_IIC1.D5
  N11: 4x20_LCD_screen_w/Green_Screen1.DB6, LCM1602_IIC1.D6
  N12: 4x20_LCD_screen_w/Green_Screen1.DB7, LCM1602_IIC1.D7
  N13: 4x20_LCD_screen_w/Green_Screen1.LED+, LCM1602_IIC1.A
  N14: 4x20_LCD_screen_w/Green_Screen1.LED-, LCM1602_IIC1.K
  N15: kEYPAD_MATRICIAL_1.col1, Part1.D41
  N16: kEYPAD_MATRICIAL_1.arrow1, Part1.D43
  N17: kEYPAD_MATRICIAL_1.col2, Part1.D45
  N18: kEYPAD_MATRICIAL_1.arrow2, Part1.D47
  N19: kEYPAD_MATRICIAL_1.col3, Part1.D49
  N20: kEYPAD_MATRICIAL_1.arrow3, Part1.D51
  N21: kEYPAD_MATRICIAL_1.arrow4, Part1.D53
  GND: LED1.cathode, LED2.cathode, Part1.GND, J1.gnd, J2.pin1, LCM1602_IIC1.GND, S1.leg0, hc-sr2.GND
  N22: LED1.anode, R1.Pin_1
  N23: LED2.anode, R2.Pin_1
  N24: R1.Pin_0, Part1.D8_PWM
  N25: R2.Pin_0, Part1.D7_PWM
  N26: Part1.D21/SCL, LCM1602_IIC1.SCL
  N27: Part1.D20/SDA, LCM1602_IIC1.SDA
  N28: Part1.D12_PWM, hc-sr2.Trig
  N29: Part1.D11_PWM, hc-sr2.Echo
  N30: Part1.D9_PWM, J1.pulse
  VCC: Part1.5V, J1.vcc, LCM1602_IIC1.VCC, hc-sr2.VCC
  N31: Part1.D5_PWM, S1.leg1
  N32: Part1.D6_PWM, J2.pin2
  N33: Part2.D21/SCL, LCM1602_IIC2.SCL
  N34: Part2.D20/SDA, LCM1602_IIC2.SDA
  GND_2: Part2.GND, LED3.cathode, LED4.cathode, J3.gnd, J4.pin1, LCM1602_IIC2.GND, S2.leg0, hc-sr3.GND
  N35: Part2.D12_PWM, hc-sr3.Trig
  N36: Part2.D11_PWM, hc-sr3.Echo
  N37: Part2.D9_PWM, J3.pulse
  N38: Part2.D8_PWM, R3.Pin_0
  VCC_2: Part2.5V, J3.vcc, LCM1602_IIC2.VCC, hc-sr3.VCC
  N39: Part2.D5_PWM, S2.leg1
  N40: Part2.D6_PWM, J4.pin2
  N41: Part2.D7_PWM, R4.Pin_0
  N42: Part2.D39, Keypad4x1.Pin1
  N43: Part2.D41, Keypad4x1.Pin2
  N44: Part2.D43, Keypad4x1.Pin3
  N45: Part2.D45, Keypad4x1.Pin4
  N46: Part2.D47, Keypad4x1.Pin5
  N47: Part2.D49, Keypad4x1.Pin6
  N48: Part2.D51, Keypad4x1.Pin7
  N49: Part2.D53, Keypad4x1.Pin8
  VSS_2: 4x20_LCD_screen_w/Green_Screen2.VSS, LCM1602_IIC2.VSS
  VDD_2: 4x20_LCD_screen_w/Green_Screen2.VDD, LCM1602_IIC2.VDD
  N50: 4x20_LCD_screen_w/Green_Screen2.V0, LCM1602_IIC2.V0
  N51: 4x20_LCD_screen_w/Green_Screen2.RS, LCM1602_IIC2.RS
  N52: 4x20_LCD_screen_w/Green_Screen2.R/W, LCM1602_IIC2.RW
  N53: 4x20_LCD_screen_w/Green_Screen2.E, LCM1602_IIC2.E
  N54: 4x20_LCD_screen_w/Green_Screen2.DB0, LCM1602_IIC2.D0
  N55: 4x20_LCD_screen_w/Green_Screen2.DB1, LCM1602_IIC2.D1
  N56: 4x20_LCD_screen_w/Green_Screen2.DB2, LCM1602_IIC2.D2
  N57: 4x20_LCD_screen_w/Green_Screen2.DB3, LCM1602_IIC2.D3
  N58: 4x20_LCD_screen_w/Green_Screen2.DB4, LCM1602_IIC2.D4
  N59: 4x20_LCD_screen_w/Green_Screen2.DB5, LCM1602_IIC2.D5
  N60: 4x20_LCD_screen_w/Green_Screen2.DB6, LCM1602_IIC2.D6
  N61: 4x20_LCD_screen_w/Green_Screen2.DB7, LCM1602_IIC2.D7
  N62: 4x20_LCD_screen_w/Green_Screen2.LED+, LCM1602_IIC2.A
  N63: 4x20_LCD_screen_w/Green_Screen2.LED-, LCM1602_IIC2.K
  N64: LED3.anode, R3.Pin_1
  N65: LED4.anode, R4.Pin_1

custom parts:
  4x20 LCD screen w/Green Screen: A standard character display with 4x20 characters.
  KEYPAD 4x3: KEYPAD matricial de 12 botones, 4 filas x 3 columnas
  LCM1602 IIC: I2C-Module to use a 1602 or 2004 LCD on with the wire.h libory Serial LCD Modul
  Keypad Membran 4x4: Membrane Keypad 4x4 Matrix
